// Logisim project basic.circ as structural Verilog: 8 circuits, main circuit main
module main (
);

  tor tor_1 ();  // open: a, b, q
  tand tand_1 ();  // open: a, b, q
endmodule

module tand (
  input  [1:0] a,
  input  [1:0] b,
  output [1:0] q
);

  or or_1 (q[1], a[1], b[1]);
  and and_1 (q[0], ~a[1], a[0], ~b[1], b[0]);  // AND_Gate
endmodule

module tor (
  input  [1:0] a,
  input  [1:0] b,
  output [1:0] q
);

  and and_1 (q[1], a[1], b[1]);
  or or_1 (q[0], a[0], b[0]);
endmodule

module tnot (
  input  [1:0] a,
  output [1:0] q
);


  assign q = {a[0], a[1]};
endmodule

module THA (
  input  [1:0] a,
  input  [1:0] b,
  output [1:0] q,
  output [1:0] carry
);

  wire and_1_out, and_2_out, and_3_out, and_4_out, and_5_out, and_6_out, not_1_out, not_2_out, not_3_out,
       not_4_out;

  not not_1 (not_1_out, a[1]);
  not not_2 (not_2_out, a[0]);
  not not_3 (not_3_out, b[1]);
  not not_4 (not_4_out, b[0]);
  and and_1 (and_1_out, not_1_out, not_2_out, b[1]);
  and and_2 (and_2_out, a[0], b[0]);
  and and_3 (and_3_out, a[1], not_3_out, not_4_out);
  and and_4 (and_4_out, not_1_out, not_2_out, b[0]);
  and and_5 (and_5_out, a[0], not_3_out, not_4_out);
  and and_6 (and_6_out, a[1], b[1]);
  and and_7 (carry[1], a[1], b[1]);
  and and_8 (carry[0], a[0], b[0]);
  or or_1 (q[1], and_1_out, and_2_out, and_3_out);
  or or_2 (q[0], and_4_out, and_5_out, and_6_out);
endmodule

module TFA (
  input  [1:0] A,
  input  [1:0] CARRY_IN,
  input  [1:0] B,
  output [1:0] CARRY_OUT,
  output [1:0] SUM
);

  wire [1:0] conv_1_x, conv_2_x, conv_3_x, tha_2_carry, tha_3_carry, tha_3_q;

  THA tha_1 (.a(tha_2_carry), .b(tha_3_carry), .q(CARRY_OUT));  // open: carry
  THA tha_2 (.a(CARRY_IN), .b(tha_3_q), .q(SUM), .carry(tha_2_carry));
  // Probe on conv_1_x
  conv conv_1 (.a(A), .x(conv_1_x));
  THA tha_3 (.a(B), .b(A), .q(tha_3_q), .carry(tha_3_carry));
  // Probe on conv_2_x
  conv conv_2 (.a(CARRY_IN), .x(conv_2_x));
  // Probe on conv_3_x
  conv conv_3 (.a(B), .x(conv_3_x));
endmodule

module conv (
  input  [1:0] a,
  output [1:0] x
);

  wire and_1_out, and_2_out, not_1_out, not_2_out;

  not not_1 (not_1_out, a[1]);
  not not_2 (not_2_out, a[0]);
  and and_1 (and_1_out, not_1_out, a[0]);
  and and_2 (and_2_out, a[1], not_2_out);
  or or_1 (x[0], and_1_out, and_2_out);

  assign x[1] = a[1];
endmodule

module adder_3trits (
  input  [5:0] in_1,
  input  [5:0] in_2,
  output [5:0] out_3
);

  wire [1:0] conv_1_x, conv_2_x, conv_3_x, conv_4_x, conv_5_x, conv_6_x, conv_7_x, conv_8_x, conv_9_x,
       tfa_2_carry_out, tfa_3_carry_out;

  // Probe on conv_1_x
  // Probe on conv_2_x
  conv conv_1 (.a(out_3[5:4]), .x(conv_1_x));
  conv conv_2 (.a(out_3[3:2]), .x(conv_2_x));
  // Probe on conv_3_x
  conv conv_3 (.a(in_1[5:4]), .x(conv_3_x));
  // Probe on conv_4_x
  conv conv_4 (.a(out_3[1:0]), .x(conv_4_x));
  conv conv_5 (.a(in_2[5:4]), .x(conv_5_x));
  // Probe on conv_5_x
  // Probe on conv_6_x
  // Probe on conv_7_x
  conv conv_6 (.a(in_1[3:2]), .x(conv_6_x));
  conv conv_7 (.a(in_1[1:0]), .x(conv_7_x));
  TFA tfa_1 (.SUM(out_3[5:4]), .A(in_1[5:4]), .B(in_2[5:4]), .CARRY_IN(tfa_2_carry_out));  // open: CARRY_OUT
  conv conv_8 (.a(in_2[3:2]), .x(conv_8_x));
  conv conv_9 (.a(in_2[1:0]), .x(conv_9_x));
  // Probe on conv_8_x
  // Probe on conv_9_x
  TFA tfa_2 (.CARRY_OUT(tfa_2_carry_out), .SUM(out_3[3:2]), .A(in_1[3:2]), .B(in_2[3:2]), .CARRY_IN(tfa_3_carry_out));
  TFA tfa_3 (.CARRY_OUT(tfa_3_carry_out), .SUM(out_3[1:0]), .A(in_1[1:0]), .B(in_2[1:0]), .CARRY_IN(2'b00));
endmodule
